# Fritzing sketch WeatherStation-Fritzing (saved by Fritzing 0.9.3b)
breadboards: 1

parts:
  NodeMCU_v1 = NodeMCU v3 LoLin [part_number=ESP8266]
  DHT1 = DHT22 Humidity and Temperature Sensor
  M1 = BME280
  R1 = Resistor [tolerance=±5% resistance=10k package="1206 [SMD]"]

nets:
  N1: NodeMCU_v1.D2, M1.SDA
  N2: NodeMCU_v1.D3, M1.SCL
  3V3: NodeMCU_v1.3V3, DHT1.VDD, M1.VIN, R1.Pin_0
  GND: NodeMCU_v1.GND#6, NodeMCU_v1.GND#13, NodeMCU_v1.GND#16, NodeMCU_v1.GND#33, DHT1.GND, M1.GND
  N3: NodeMCU_v1.D5, DHT1.DATA, R1.Pin_1

custom parts:
  NodeMCU v3 LoLin: NodeMCU v3 LoLin NodeMCU (http://www.nodemcu.com/) is an open source IoT platform. It includes firmware (https://nodemcu-build.com/) which runs on the ESP8266 Wi-Fi SoC from Espressif Systems, and hardware which is based on the ESP-12E module. The term "NodeMCU" by default refers to the firmware rather than the dev kits. The firmware uses the Lua scripting language. It is based on the eLua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
  BME280: Temperature Humidity Barometric presure Sensor
